// Digital circuit ULA.dig as structural Verilog
module ULA (
  input  [7:0] A,
  input  [7:0] B,
  input  [2:0] ALUOp,
  output [7:0] S
);

  wire [7:0] add_1_s, DEC_s, INC_s, LOAD_s, mul_1_mul, sub_1_s;

  Add #(.Bits(8)) LOAD (.a(A), .b({8{1'b0}}), .c_i(1'b0), .s(LOAD_s));  // open: c_o
  Add #(.Bits(8)) add_1 (.a(A), .b(B), .c_i(1'b0), .s(add_1_s));  // open: c_o
  Sub #(.Bits(8)) sub_1 (.a(A), .b(B), .c_i(1'b0), .s(sub_1_s));  // open: c_o
  Add #(.Bits(8)) INC (.a(A), .b(8'h1), .c_i(1'b0), .s(INC_s));  // open: c_o
  Sub #(.Bits(8)) DEC (.a(A), .b(8'h1), .c_i(1'b0), .s(DEC_s));  // open: c_o
  Mul #(.Bits(4)) mul_1 (.a(A[3:0]), .b(B[3:0]), .mul(mul_1_mul));
  Multiplexer #(.Selector_Bits(3), .Bits(8)) multiplexer_1 (
    .sel(ALUOp), .in_0(LOAD_s), .in_1(add_1_s), .in_2(sub_1_s), .in_3(INC_s), .in_4(DEC_s), .in_5(mul_1_mul),
    .in_6({8{1'b0}}), .in_7({8{1'b0}}), .out(S));

  // Other names for the same wires on the sheet: Ain[7:0] = A; Bin[7:0] = B; Op[2:0] = ALUOp
endmodule
