// Digital circuit cpu_rom.dig as structural Verilog
module cpu_rom (
  input  clk
);

  wire PCen, t_ff_1_nq;
  wire [2:0] UC_d;
  wire [3:0] SEin;
  wire [7:0] ACCQ, PC_out, SEout, ULAS;
  wire [7:4] rom_1_d;

  Counter #(.Bits(8)) PC (.en(PCen), .C(clk), .clr(1'b0), .out(PC_out));  // open: ovf
  T_FF t_ff_1 (.T(1'b1), .C(clk), .Q(PCen), .nQ(t_ff_1_nq));
  ROM #(.AddrBits(8), .Bits(8)) rom_1 (.A(PC_out), .sel(1'b0), .D({rom_1_d, SEin}));
  Register #(.Bits(8)) ACC (.D(ULAS), .C(clk), .en(t_ff_1_nq), .Q(ACCQ));
  ROM #(.AddrBits(4), .Bits(3)) UC (.A(rom_1_d), .sel(1'b0), .D(UC_d));
  BitExtender #(.inputBits(4), .outputBits(8)) bitextender_1 (.in(SEin), .out(SEout));
  ULA ula_1 (.A(ACCQ), .B(SEout), .ALUOp(UC_d), .S(ULAS));
  Seven_Seg_Hex seven_seg_hex_1 (.d(ACCQ[3:0]), .dp(1'b0));
  Seven_Seg_Hex seven_seg_hex_2 (.d(ACCQ[7:4]), .dp(1'b0));

  // Notes on the sheet:
  //   contents of rom_1 (hex, n*v repeats v):
  //   5,3,2,21,0,1
  //   contents of UC (hex, n*v repeats v):
  //   0,1,2,3,4,5
endmodule
